# Fritzing sketch Waveform-Generator (saved by Fritzing 0.9.9b)
perfboards: 1

parts:
  Mod1 = Raspberry Pi Pico
  R44 = Resistor [tolerance=±1% power=0.25 resistance=4.7k package=THT]
  R45 = Resistor [tolerance=±1% power=0.25 resistance=4.7k package=THT]
  R46 = Resistor [tolerance=±1% power=0.25 resistance=4.7k package=THT]
  R47 = Resistor [tolerance=±1% power=0.25 resistance=4.7k package=THT]
  R48 = Resistor [tolerance=±1% power=0.25 resistance=4.7k package=THT]
  R49 = Resistor [tolerance=±1% power=0.25 resistance=4.7k package=THT]
  R50 = Resistor [tolerance=±1% power=0.25 resistance=4.7k package=THT]
  R51 = Resistor [tolerance=±1% power=0.25 resistance=4.7k package=THT]
  R52 = Resistor [tolerance=±1% power=0.25 resistance=4.7k package=THT]
  R53 = Resistor [tolerance=±1% power=0.25 resistance=4.7k package=THT]
  R54 = Resistor [tolerance=±1% power=0.25 resistance=4.7k package=THT]
  R55 = Resistor [tolerance=±1% power=0.25 resistance=4.7k package=THT]
  R56 = Resistor [tolerance=±1% power=0.25 resistance=4.7k package=THT]
  R57 = Resistor [tolerance=±1% power=0.25 resistance=4.7k package=THT]
  R58 = Resistor [tolerance=±1% power=0.25 resistance=4.7k package=THT]
  R59 = Resistor [tolerance=±1% power=0.25 resistance=4.7k package=THT]
  R60 = Resistor [tolerance=±1% power=0.25 resistance=4.7k package=THT]
  R61 = Resistor [tolerance=±1% power=0.25 resistance=4.7k package=THT]
  R62 = Resistor [tolerance=±1% power=0.25 resistance=4.7k package=THT]
  R63 = Resistor [tolerance=±1% power=0.25 resistance=4.7k package=THT]
  R64 = Resistor [tolerance=±1% power=0.25 resistance=4.7k package=THT]
  R65 = Resistor [tolerance=±1% power=0.25 resistance=4.7k package=THT]
  R66 = Resistor [tolerance=±1% power=0.25 resistance=4.7k package=THT]
  R67 = Resistor [tolerance=±1% power=0.25 resistance=4.7k package=THT]
  R68 = Resistor [tolerance=±1% power=0.25 resistance=4.7k package=THT]
  LM358 = LM 358 Dual Op-Amp [package="DIP8 [THT]"]
  +OUT = BANANA_CONN [package=banana_conn]
  GND = BANANA_CONN [package=banana_conn]
  Waveform = Rotary Encoder with Knob
  Frequency = Rotary Encoder with Knob
  OLED_I2C_128x64 = OLED 128x64 I2C Monochrome Display

nets:
  N1: Mod1.pin_1, R44.Pin_0
  N2: Mod1.pin_2, R50.Pin_0
  N3: Mod1.pin_3, Mod1.pin_8, Mod1.pin_13, Mod1.pin_18, Mod1.pin_23, Mod1.pin_28, Mod1.pin_33, Mod1.pin_38, Mod1.pin_42, R49.Pin_1, LM358.connector2, LM358.connector3, GND.1, Waveform.no_name_yet#3, Waveform.no_name_yet#5, Frequency.no_name_yet#3, Frequency.no_name_yet#5, OLED_I2C_128x64.GND
  N4: Mod1.pin_4, R52.Pin_0
  N5: Mod1.pin_5, R51.Pin_0
  N6: Mod1.pin_6, R54.Pin_0
  N7: Mod1.pin_7, R53.Pin_0
  N8: Mod1.pin_9, R56.Pin_0
  N9: Mod1.pin_10, R55.Pin_0
  N10: Mod1.pin_21, OLED_I2C_128x64.SDA
  N11: Mod1.pin_22, OLED_I2C_128x64.SCK
  N12: Mod1.pin_26, Frequency.no_name_yet#4
  N13: Mod1.pin_27, Frequency.no_name_yet#2
  N14: Mod1.pin_29, Frequency.no_name_yet#1
  N15: Mod1.pin_31, Waveform.no_name_yet#4
  N16: Mod1.pin_32, Waveform.no_name_yet#2
  N17: Mod1.pin_34, Waveform.no_name_yet#1
  N18: Mod1.pin_36, OLED_I2C_128x64.VDD
  N19: Mod1.pin_40, LM358.connector7
  N20: R44.Pin_1, R45.Pin_0, R46.Pin_0, R49.Pin_0
  N21: R45.Pin_1, R46.Pin_1, R47.Pin_0, R48.Pin_0, R50.Pin_1
  N22: R47.Pin_1, R48.Pin_1, R52.Pin_1, R57.Pin_0, R59.Pin_0
  N23: R51.Pin_1, R57.Pin_1, R58.Pin_0, R59.Pin_1, R60.Pin_0
  N24: R53.Pin_1, R61.Pin_1, R62.Pin_0, R63.Pin_1, R64.Pin_0
  N25: R54.Pin_1, R58.Pin_1, R60.Pin_1, R61.Pin_0, R63.Pin_0
  N26: R55.Pin_1, R65.Pin_1, R66.Pin_0, R67.Pin_1, R68.Pin_0, LM358.connector1
  N27: R56.Pin_1, R62.Pin_1, R64.Pin_1, R65.Pin_0, R67.Pin_0
  N28: R66.Pin_1, R68.Pin_1, LM358.connector0, +OUT.1

notes:
  All resistors are 4K7 1%
  (unused)

custom parts:
  Raspberry Pi Pico: Raspberry Pi Pico. Based around the RP2040 microcontroller the Pico is a low cost microcontroller device bringing Raspberry Pi quality, cost, and easy of use to the microcontroller space. Jan 2021, Split part in to two versions: tht (this one) and SMD. This one will drill holes for a .1 in header in pcb to allow plugging in the module as well as providing pads to solder the module to the top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
  Rotary Encoder with Knob: Rotary Encoder with 1/4" Shaft and Knob
